// Logisim project Circuitos Sequenciais.circ as structural Verilog: 13 circuits, main circuit RS
module RS (
  input  R,
  input  S,
  output Q,
  output Q_prime
);

  nor nor_1 (Q, R, Q_prime);
  nor nor_2 (Q_prime, Q, S);
endmodule

module RS_Clock (
  input  R,
  input  Clock,
  input  S,
  output Q,
  output Q_prime
);

  wire and_1_out, and_2_out;

  and and_1 (and_1_out, R, Clock);
  and and_2 (and_2_out, Clock, S);
  nor nor_1 (Q, and_1_out, Q_prime);
  nor nor_2 (Q_prime, Q, and_2_out);
endmodule

module D (
  input  Clock,
  input  D,
  output Q,
  output Q_prime
);

  wire and_1_out, and_2_out, not_1_out;

  not not_1 (not_1_out, D);
  and and_1 (and_1_out, not_1_out, Clock);
  and and_2 (and_2_out, Clock, D);
  nor nor_1 (Q, and_1_out, Q_prime);
  nor nor_2 (Q_prime, Q, and_2_out);
endmodule

module JK (
  input  K,
  input  Clock,
  input  J,
  output Q,
  output Q_prime
);

  wire and_1_out, and_2_out;

  and and_1 (and_1_out, Q, K, Clock);
  and and_2 (and_2_out, Clock, J, Q_prime);
  nor nor_1 (Q, and_1_out, Q_prime);
  nor nor_2 (Q_prime, Q, and_2_out);
endmodule

module FlipFlopD (
  input  Clock,
  input  D,
  output Q,
  output Q_prime
);

  D_Flip_Flop d_ff_1 (.clk(Clock), .D(D), .Q(Q), .Qn(Q_prime), .preset(1'b0), .en(1'b1), .reset(1'b0));
endmodule

module FlipFlopJK (
  input  J,
  input  Clock,
  input  K,
  output Q,
  output Q_prime
);

  J_K_Flip_Flop #(.trigger("falling")) j_k_ff_1 (
    .J(J), .clk(Clock), .K(K), .Q(Q), .Qn(Q_prime), .preset(1'b0), .en(1'b1), .reset(1'b0));
endmodule

module FlipFlopJK_Clear (
  input  J,
  input  Clock,
  input  K,
  input  Clear,
  output Q,
  output Q_prime
);

  J_K_Flip_Flop #(.trigger("falling")) j_k_ff_1 (
    .J(J), .clk(Clock), .K(K), .Q(Q), .Qn(Q_prime), .preset(1'b0), .en(1'b1), .reset(Clear));
endmodule

module registrador_paralelo_8_bits (
  input  E7,
  input  E6,
  input  E5,
  input  E4,
  input  E3,
  input  E2,
  input  E1,
  input  E0,
  input  Load,
  output out_10,
  output out_11,
  output out_12,
  output out_13,
  output out_14,
  output out_15,
  output out_16,
  output out_17
);

  wire and_1_out, clock_1_out;

  Clock clock_1 (.out(clock_1_out));
  and and_1 (and_1_out, clock_1_out, Load);
  FlipFlopD flipflopd_1 (.Clock(and_1_out), .D(E7), .Q(out_10));  // open: Q_prime
  FlipFlopD flipflopd_2 (.Clock(and_1_out), .D(E6), .Q(out_11));  // open: Q_prime
  FlipFlopD flipflopd_3 (.Clock(and_1_out), .D(E5), .Q(out_12));  // open: Q_prime
  FlipFlopD flipflopd_4 (.Clock(and_1_out), .D(E4), .Q(out_13));  // open: Q_prime
  FlipFlopD flipflopd_5 (.Clock(and_1_out), .D(E3), .Q(out_14));  // open: Q_prime
  FlipFlopD flipflopd_6 (.Clock(and_1_out), .D(E2), .Q(out_15));  // open: Q_prime
  FlipFlopD flipflopd_7 (.Clock(and_1_out), .D(E1), .Q(out_16));  // open: Q_prime
  FlipFlopD flipflopd_8 (.Clock(and_1_out), .D(E0), .Q(out_17));  // open: Q_prime
endmodule

module registrador_deslocamento (
  input  E7,
  output out_2,
  output out_3,
  output out_4,
  output out_5,
  output out_6
);

  wire clock_1_out;

  Clock clock_1 (.out(clock_1_out));
  FlipFlopD flipflopd_1 (.Clock(clock_1_out), .D(E7), .Q(out_2));  // open: Q_prime
  FlipFlopD flipflopd_2 (.Clock(clock_1_out), .D(out_2), .Q(out_3));  // open: Q_prime
  FlipFlopD flipflopd_3 (.Clock(clock_1_out), .D(out_3), .Q(out_4));  // open: Q_prime
  FlipFlopD flipflopd_4 (.Clock(clock_1_out), .D(out_4), .Q(out_5));  // open: Q_prime
  FlipFlopD flipflopd_5 (.Clock(clock_1_out), .D(out_5), .Q(out_6));  // open: Q_prime
endmodule

module Contador4bits (
  input  in_1
);

  wire clock_1_out, clock_2_out, n4bitsadder_1_p7, n4bitsadder_1_p9, n4bitsadder_1_p11, n4bitsadder_1_p12,
       not_1_out;
  wire [3:0] flipflopjk_1_q, n4bitsadder_1_p13;

  Clock clock_1 (.out(clock_1_out));
  not not_1 (not_1_out, clock_1_out);
  Clock clock_2 (.out(clock_2_out));
  // _4bitsadder 4bitsadder_1: pin names not known; wires that end beside it: 1'b0, 1'b0, 1'b0, not_1_out, n4bitsadder_1_p13[3], n4bitsadder_1_p13[2], n4bitsadder_1_p7, n4bitsadder_1_p13[2], n4bitsadder_1_p9, n4bitsadder_1_p13[1], n4bitsadder_1_p11, n4bitsadder_1_p12, n4bitsadder_1_p13[0]
  Hex_Digit_Display hex_digit_display_1 (.value(n4bitsadder_1_p13));  // open: dp
  FlipFlopJK flipflopjk_1 (.J(in_1), .Clock(clock_2_out), .K(in_1), .Q(flipflopjk_1_q[0]));  // open: Q_prime
  FlipFlopD flipflopd_1 (.Clock(clock_1_out), .D(n4bitsadder_1_p13[0]), .Q(n4bitsadder_1_p12));  // open: Q_prime
  FlipFlopJK flipflopjk_2 (.J(in_1), .Clock(flipflopjk_1_q[0]), .K(in_1), .Q(flipflopjk_1_q[1]));  // open: Q_prime
  FlipFlopD flipflopd_2 (.Clock(clock_1_out), .D(n4bitsadder_1_p13[1]), .Q(n4bitsadder_1_p11));  // open: Q_prime
  FlipFlopJK flipflopjk_3 (.J(in_1), .Clock(flipflopjk_1_q[1]), .K(in_1), .Q(flipflopjk_1_q[2]));  // open: Q_prime
  Hex_Digit_Display hex_digit_display_2 (.value(flipflopjk_1_q));  // open: dp
  FlipFlopD flipflopd_3 (.Clock(clock_1_out), .D(n4bitsadder_1_p13[2]), .Q(n4bitsadder_1_p9));  // open: Q_prime
  FlipFlopJK flipflopjk_4 (.J(in_1), .Clock(flipflopjk_1_q[2]), .K(in_1), .Q(flipflopjk_1_q[3]));  // open: Q_prime
  FlipFlopD flipflopd_4 (.Clock(clock_1_out), .D(n4bitsadder_1_p13[3]), .Q(n4bitsadder_1_p7));  // open: Q_prime
endmodule

module Contador8bits (
  input  in_1
);

  wire and_1_out, clock_1_out;
  wire [3:0] flipflopjk_1_q, flipflopjk_2_q;

  Clock clock_1 (.out(clock_1_out));
  FlipFlopJK flipflopjk_1 (.J(1'b1), .Clock(and_1_out), .K(1'b1), .Q(flipflopjk_1_q[0]));  // open: Q_prime
  FlipFlopJK flipflopjk_2 (.J(in_1), .Clock(clock_1_out), .K(in_1), .Q(flipflopjk_2_q[0]));  // open: Q_prime
  and and_1 (and_1_out, flipflopjk_2_q[0], flipflopjk_2_q[1], flipflopjk_2_q[2], flipflopjk_2_q[3]);
  FlipFlopJK flipflopjk_3 (.J(1'b1), .Clock(flipflopjk_1_q[0]), .K(1'b1), .Q(flipflopjk_1_q[1]));  // open: Q_prime
  FlipFlopJK flipflopjk_4 (.J(in_1), .Clock(flipflopjk_2_q[0]), .K(in_1), .Q(flipflopjk_2_q[1]));  // open: Q_prime
  FlipFlopJK flipflopjk_5 (.J(1'b1), .Clock(flipflopjk_1_q[1]), .K(1'b1), .Q(flipflopjk_1_q[2]));  // open: Q_prime
  FlipFlopJK flipflopjk_6 (.J(in_1), .Clock(flipflopjk_2_q[1]), .K(in_1), .Q(flipflopjk_2_q[2]));  // open: Q_prime
  Hex_Digit_Display hex_digit_display_1 (.value(flipflopjk_1_q));  // open: dp
  FlipFlopJK flipflopjk_7 (.J(1'b1), .Clock(flipflopjk_1_q[2]), .K(1'b1), .Q(flipflopjk_1_q[3]));  // open: Q_prime
  FlipFlopJK flipflopjk_8 (.J(in_1), .Clock(flipflopjk_2_q[2]), .K(in_1), .Q(flipflopjk_2_q[3]));  // open: Q_prime
  Hex_Digit_Display hex_digit_display_2 (.value(flipflopjk_2_q));  // open: dp
endmodule

module ContadorDecimal (
  input  in_1
);

  wire and_1_out, and_2_out, and_3_out, clock_1_out;
  wire [3:0] flipflopjk_clear_1_q, flipflopjk_clear_2_q;

  and and_1 (and_1_out, ~flipflopjk_clear_1_q[0], flipflopjk_clear_1_q[1], ~flipflopjk_clear_1_q[2], flipflopjk_clear_1_q[3]);  // AND_Gate
  Clock clock_1 (.out(clock_1_out));
  FlipFlopJK_Clear flipflopjk_clear_1 (
    .J(1'b1), .Clock(and_3_out), .K(1'b1), .Clear(and_1_out), .Q(flipflopjk_clear_1_q[0]));  // open: Q_prime
  FlipFlopJK_Clear flipflopjk_clear_2 (
    .J(in_1), .Clock(clock_1_out), .K(in_1), .Clear(and_2_out), .Q(flipflopjk_clear_2_q[0]));  // open: Q_prime
  and and_2 (and_2_out, ~flipflopjk_clear_2_q[0], flipflopjk_clear_2_q[1], ~flipflopjk_clear_2_q[2], flipflopjk_clear_2_q[3]);  // AND_Gate
  and and_3 (and_3_out, flipflopjk_clear_2_q[3], ~flipflopjk_clear_2_q[2], ~flipflopjk_clear_2_q[1], flipflopjk_clear_2_q[0]);  // AND_Gate
  FlipFlopJK_Clear flipflopjk_clear_3 (
    .J(1'b1), .Clock(flipflopjk_clear_1_q[0]), .K(1'b1), .Clear(and_1_out), .Q(flipflopjk_clear_1_q[1]));  // open: Q_prime
  FlipFlopJK_Clear flipflopjk_clear_4 (
    .J(in_1), .Clock(flipflopjk_clear_2_q[0]), .K(in_1), .Clear(and_2_out), .Q(flipflopjk_clear_2_q[1]));  // open: Q_prime
  FlipFlopJK_Clear flipflopjk_clear_5 (
    .J(1'b1), .Clock(flipflopjk_clear_1_q[1]), .K(1'b1), .Clear(and_1_out), .Q(flipflopjk_clear_1_q[2]));  // open: Q_prime
  FlipFlopJK_Clear flipflopjk_clear_6 (
    .J(in_1), .Clock(flipflopjk_clear_2_q[1]), .K(in_1), .Clear(and_2_out), .Q(flipflopjk_clear_2_q[2]));  // open: Q_prime
  Hex_Digit_Display hex_digit_display_1 (.value(flipflopjk_clear_1_q));  // open: dp
  FlipFlopJK_Clear flipflopjk_clear_7 (
    .J(1'b1), .Clock(flipflopjk_clear_1_q[2]), .K(1'b1), .Clear(and_1_out), .Q(flipflopjk_clear_1_q[3]));  // open: Q_prime
  FlipFlopJK_Clear flipflopjk_clear_8 (
    .J(in_1), .Clock(flipflopjk_clear_2_q[2]), .K(in_1), .Clear(and_2_out), .Q(flipflopjk_clear_2_q[3]));  // open: Q_prime
  Hex_Digit_Display hex_digit_display_2 (.value(flipflopjk_clear_2_q));  // open: dp
endmodule

module contador_decimal_com_ROM (
  input  in_1
);

  wire and_1_out, clock_1_out;
  wire [7:0] flipflopjk_2_q;
  wire [11:0] rom_1_data;

  Clock clock_1 (.out(clock_1_out));
  FlipFlopJK flipflopjk_1 (.J(1'b1), .Clock(and_1_out), .K(1'b1), .Q(flipflopjk_2_q[4]));  // open: Q_prime
  FlipFlopJK flipflopjk_2 (.J(in_1), .Clock(clock_1_out), .K(in_1), .Q(flipflopjk_2_q[0]));  // open: Q_prime
  and and_1 (and_1_out, flipflopjk_2_q[0], flipflopjk_2_q[1], flipflopjk_2_q[2], flipflopjk_2_q[3]);
  FlipFlopJK flipflopjk_3 (.J(1'b1), .Clock(flipflopjk_2_q[4]), .K(1'b1), .Q(flipflopjk_2_q[5]));  // open: Q_prime
  FlipFlopJK flipflopjk_4 (.J(in_1), .Clock(flipflopjk_2_q[0]), .K(in_1), .Q(flipflopjk_2_q[1]));  // open: Q_prime
  FlipFlopJK flipflopjk_5 (.J(1'b1), .Clock(flipflopjk_2_q[5]), .K(1'b1), .Q(flipflopjk_2_q[6]));  // open: Q_prime
  FlipFlopJK flipflopjk_6 (.J(in_1), .Clock(flipflopjk_2_q[1]), .K(in_1), .Q(flipflopjk_2_q[2]));  // open: Q_prime
  FlipFlopJK flipflopjk_7 (.J(1'b1), .Clock(flipflopjk_2_q[6]), .K(1'b1), .Q(flipflopjk_2_q[7]));  // open: Q_prime
  ROM #(.dataWidth(12)) rom_1 (.addr(flipflopjk_2_q), .data(rom_1_data));  // open: sel
  FlipFlopJK flipflopjk_8 (.J(in_1), .Clock(flipflopjk_2_q[2]), .K(in_1), .Q(flipflopjk_2_q[3]));  // open: Q_prime
  Hex_Digit_Display hex_digit_display_1 (.value(rom_1_data[11:8]));  // open: dp
  Hex_Digit_Display hex_digit_display_2 (.value(rom_1_data[3:0]));  // open: dp
  Hex_Digit_Display hex_digit_display_3 (.value(rom_1_data[7:4]));  // open: dp

  // Notes on the sheet:
  //   contents of rom_1 (hex, n*v repeats v):
  //   0 1 2 3 4 5 6 7 8 9 10 11 12 13 14 15 16 17 18 19 20 21 22 23 24 25 26 27 28 29 30 31 32 33 34 35 36
  //   37 38 39 40 41 42 43 44 45 46 47 48 49 50 51 52 53 54 55 56 57 58 59 60 61 62 63 64 65 66 67 68 69
  //   70 71 72 73 74 75 76 77 78 79 80 81 82 83 84 85 86 87 88 89 90 91 92 93 94 95 96 97 98 99 100 101
  //   102 103 104 105 106 107 108 109 110 111 112 113 114 115 116 117 118 119 120 121 122 123 124 125 126
  //   127 128 129 130 131 132 133 134 135 136 137 138 139 140 141 142 143 144 145 146 147 148 149 150 151
  //   152 153 154 155 156 157 158 159 160 161 162 163 164 165 166 167 168 169 170 171 172 173 174 175 176
  //   177 178 179 180 181 182 183 184 185 186 187 188 189 190 191 192 193 194 195 196 197 198 199 200 201
  //   202 203 204 205 206 207 208 209 210 211 212 213 214 215 216 217 218 219 220 221 222 223 224 225 226
  //   227 228 229 230 231 232 233 234 235 236 237 238 239 240 241 242 243 244 245 246 247 248 249 250 251
  //   252 253 254 255
endmodule
